# Fritzing sketch Final (saved by Fritzing 0.9.5d)
circuit board: 8.46667cm x 5.64444cm
breadboards: 1

parts:
  R1 = Resistor [tolerance=±5% resistance=220 package=THT]
  S1 = Momentary Switch [package=ksa_sealed_tac_switch]
  S2 = Momentary Switch [package=ksa_sealed_tac_switch]
  R2 = Resistor [tolerance=±5% resistance=220 package="2010 [SMD]"]
  S3 = Momentary Switch [package=ksa_sealed_tac_switch]
  R3 = Resistor [tolerance=±5% resistance=220 package="2010 [SMD]"]
  S4 = Momentary Switch [package=ksa_sealed_tac_switch]
  R4 = Resistor [tolerance=±5% resistance=220 package="2010 [SMD]"]
  S5 = Momentary Switch [package=ksa_sealed_tac_switch]
  S6 = Momentary Switch [package=ksa_sealed_tac_switch]
  R5 = Resistor [tolerance=±5% resistance=220 package="2010 [SMD]"]
  R6 = Resistor [tolerance=±5% resistance=220 package="2010 [SMD]"]
  S7 = Momentary Switch [package=ksa_sealed_tac_switch]
  R7 = Resistor [tolerance=±5% resistance=220 package="2010 [SMD]"]
  S8 = Momentary Switch [package=ksa_sealed_tac_switch]
  R8 = Resistor [tolerance=±5% resistance=220 package="2010 [SMD]"]
  S9 = Momentary Switch [package=ksa_sealed_tac_switch]
  R9 = Resistor [tolerance=±5% resistance=220 package="2010 [SMD]"]
  S10 = Momentary Switch [package=ksa_sealed_tac_switch]
  R10 = Resistor [tolerance=±5% resistance=220 package="2010 [SMD]"]
  Part2 = Arduino Mega 2560 (Rev3)
  S11 = Momentary Switch [package=ksa_sealed_tac_switch]
  R11 = Resistor [tolerance=±5% resistance=220 package="2010 [SMD]"]
  S12 = Momentary Switch [package=ksa_sealed_tac_switch]
  R12 = Resistor [tolerance=±5% resistance=220 package="2010 [SMD]"]
  S13 = Momentary Switch [package=ksa_sealed_tac_switch]
  R13 = Resistor [tolerance=±5% resistance=220 package="2010 [SMD]"]
  S14 = Momentary Switch [package=ksa_sealed_tac_switch]
  S15 = Momentary Switch [package=ksa_sealed_tac_switch]
  S16 = Momentary Switch [package=ksa_sealed_tac_switch]
  S17 = Momentary Switch [package=ksa_sealed_tac_switch]
  S18 = Momentary Switch [package=ksa_sealed_tac_switch]
  S19 = Momentary Switch [package=ksa_sealed_tac_switch]
  S20 = Momentary Switch [package=ksa_sealed_tac_switch]
  S21 = Momentary Switch [package=ksa_sealed_tac_switch]
  S22 = Momentary Switch [package=ksa_sealed_tac_switch]
  R14 = Resistor [tolerance=±5% resistance=220 package="2010 [SMD]"]
  R15 = Resistor [tolerance=±5% resistance=220 package="2010 [SMD]"]
  R16 = Resistor [tolerance=±5% resistance=220 package="2010 [SMD]"]
  R17 = Resistor [tolerance=±5% resistance=220 package="2010 [SMD]"]
  R18 = Resistor [tolerance=±5% resistance=220 package="2010 [SMD]"]
  R19 = Resistor [tolerance=±5% resistance=220 package="2010 [SMD]"]
  R20 = Resistor [tolerance=±5% resistance=220 package="2010 [SMD]"]
  R21 = Resistor [tolerance=±5% resistance=220 package="2010 [SMD]"]
  R22 = Resistor [tolerance=±5% resistance=220 package="2010 [SMD]"]
  S25 = Toggle Switch [package=switch-spst-smd-a]
  S26 = Toggle Switch [package=switch-spst-smd-a]
  S27 = Toggle Switch [package=switch-spst-smd-a]
  S28 = Toggle Switch [package=switch-spst-smd-a]
  S29 = Toggle Switch [package=switch-spst-smd-a]
  S30 = Toggle Switch [package=switch-spst-smd-a]
  U1 = SLIDER [package=slider]

nets:
  N1: R1.Pin_0, R3.Pin_0, R4.Pin_0, R5.Pin_0, R7.Pin_0, R8.Pin_0, R9.Pin_0, R10.Pin_0, Part2.GND, R12.Pin_0, R13.Pin_1, R14.Pin_1, R15.Pin_1, R16.Pin_1, R17.Pin_1, R18.Pin_1, R19.Pin_1, R20.Pin_1, R21.Pin_1, R22.Pin_1, S25.O, S26.O, S27.O, S28.O, S29.O, S30.O, U1.E
  N2: R1.Pin_1, S1.2, Part2.D0_RX0
  N3: S1.4, S2.4, R2.Pin_0, S3.4, S4.4, S5.4, S6.4, R6.Pin_0, S7.4, S8.4, S9.4, S10.4, Part2.3V3, S11.4, R11.Pin_0, S12.4, S13.1, S14.1, S15.1, S16.1, S17.1, S18.1, S19.1, S20.1, S21.1, S22.1, S25.P, S26.P, S27.P, S28.P, S29.P, S30.P, U1.A
  N4: S2.2, R2.Pin_1, Part2.D1_TX0
  N5: S3.2, R3.Pin_1, Part2.D2_PWM
  N6: S4.2, R4.Pin_1, Part2.D5_PWM
  N7: S5.2, R5.Pin_1, Part2.D3_PWM
  N8: S6.2, R6.Pin_1, Part2.D4_PWM
  N9: S7.2, R7.Pin_1, Part2.D6_PWM
  N10: S8.2, R8.Pin_1, Part2.D7_PWM
  N11: S9.2, R9.Pin_1, Part2.D8_PWM
  N12: S10.2, R10.Pin_1, Part2.D9_PWM
  N13: Part2.A0, U1.S
  N14: Part2.D21/SCL, S22.3, R22.Pin_0
  N15: Part2.D20/SDA, S21.3, R21.Pin_0
  N16: Part2.D19/RX1, S20.3, R20.Pin_0
  N17: Part2.D18/TX1, S19.3, R19.Pin_0
  N18: Part2.D17_PWM/RX2, S18.3, R18.Pin_0
  N19: Part2.D16_PWM/TX2, S17.3, R17.Pin_0
  N20: Part2.D15/RX3, S16.3, R16.Pin_0
  N21: Part2.D14/TX3, S15.3, R15.Pin_0
  N22: Part2.D13_PWM, S14.3, R14.Pin_0
  N23: Part2.D12_PWM, S13.3, R13.Pin_0
  N24: Part2.D11_PWM, S12.2, R12.Pin_1
  N25: Part2.D10_PWM, S11.2, R11.Pin_1
  N26: Part2.D22, S27.S
  N27: Part2.D23, S29.S
  N28: Part2.D24, S28.S
  N29: Part2.D25, S26.S
  N30: Part2.D26, S25.S
  N31: Part2.D27, S30.S

custom parts:
  Toggle Switch: SPST Switch Simple slide switch. Spark Fun Electronics SKU : COM-00102
